# Fritzing sketch Aansluitschema (saved by Fritzing 1.0.4)
breadboards: 1

parts:
  M1 = Arduino NANO RP2040 CONNECT with headers
  OLED1 = OLED 128x64 I2C Monochrome Display
  SD-Card = Micro SD card reader
  Sensor = OLED 128x64 I2C Monochrome Display
  GPS = u-blox NEO-6M GPS Breakout
  DS3231 = OLED 128x64 I2C Monochrome Display
  S4 = Momentary Switch [package=ksa_sealed_tac_switch]
  S3 = Momentary Switch [package=ksa_sealed_tac_switch]
  S2 = Momentary Switch [package=ksa_sealed_tac_switch]
  S1 = Momentary Switch [package=ksa_sealed_tac_switch]
  Onderdeel4 = Digital FM Radio Receiver  # not connected
  Onderdeel4_2 = Digital FM Radio Receiver  # not connected
  J1 = ATX24 Pin Power Supply Connector [mn="DC DC Power" mpn="Vin 12V , OUTPUT 12V / 5V / 3.3V" package=atx24_right_angle]  # not connected
  R1 = Resistor [tolerance=±5% power=0.25W resistance=2.7k package=THT]
  R2 = Resistor [tolerance=±5% power=0.25W resistance=6.8k package=THT]
  U1 = DIODE-ZENER [mn=3.3 package=diode-zener]

nets:
  N1: M1.TX, GPS.Pin_3
  N2: M1.RX, GPS.Pin_4
  N3: M1.D4, SD-Card.Pin_2
  N4: M1.D6, S1.3
  N5: M1.D7, S2.3
  N6: M1.D8, S3.3
  N7: M1.D9, S4.3
  N8: M1.D11, SD-Card.Pin_3
  N9: M1.D12, SD-Card.Pin_5
  N10: M1.D13, SD-Card.Pin_4
  N11: M1.D18, OLED1.SDA, DS3231.VDD
  N12: M1.D19, OLED1.SCK, DS3231.GND
  3.3V: OLED1.VDD, DS3231.SCK
  5V: SD-Card.Pin_1
  GND: Sensor.VCC, Sensor.L/D, DS3231.SDA
  N13: Sensor.SDA, R1.Pin_1
  N14: R1.Pin_0, R2.Pin_1, U1.A
  PIN D3 Arduino: R2.Pin_0, U1.C

notes:
  Pinbezetting Arduino Nano ESP32-S3
  01 D1 / TX0 - TXD (GPS air530Z)
  02 D0 / RX0 - RXD (GPS Air530Z)
  03 RESET - Vout Spanningsdeler
  04 GND - GND (Multi)
  05 D2 -
  06 D3 - Interrupt Sensor
  07 D4 - CS (SD-Card)
  08 D5 -
  09 D6 - S1 (Pull-up)
  10 D7 - S2 (Pull-up)
  11 D8 - S3 (Pull-up)
  12 D9 - S4 (Pull-up)
  13 D10 -
  14 D11 / COPI - MOSI (SD-CARD)
  15 D12 / CIPO - MISO (SD-CARD)
  16 D13 / SCK - CLK (SD-CARD)
  17 3V3 - 3V3/VDD/VCC (Multi)
  18 REF -
  19 D14 (A0) -
  20 D15 (A1) -
  21 D16 (A2) -
  22 D17 (A3) -
  23 D18 (A4) - SDA (OLED / DS3231)
  24 D19 (A5) - SCK (OLED) SCL (DS3231)
  25 D20 (A6) -
  26 D21 (A7) -
  27 VUSB (OUT)-
  28 RESET -
  29 GND - GND (Multi)
  30 VIN (IN) -
  Spanningsdeler (R1 = 2.7kΩ, R2 = 6.8kΩ en Zener is 3.3)
  LogiTrack MR1, Aansluitschema van modules op Arduino Nano ESp32-S3., M van Riel

custom parts:
  Micro SD card reader: Micro SD card reader.
